// Digital circuit CPU.dig as structural Verilog
module CPU (
  input  Clock,
  input  [31:0] VemDoEXStage,
  input  PCSrc1,
  input  PCWrite,
  input  PCSrc2,
  output [31:0] VaiVirarInstMem,
  output BitIgualdade
);

  wire u_EX_MEM_2_memtoreg, u_EX_MEM_2_regwrite;
  wire [1:0] u_EX_MEM_wbsignals_out, u_ID_EX_memsignals_out, u_ID_EX_wbsignals_out,
       u_Mux_ControlSignals_memsignals_out, u_Mux_ControlSignals_wbsignals_out;
  wire [2:0] u_IF_ID_func3;
  wire [4:0] u_EX_MEM_2_rd_out, u_EX_MEM_rd_out, u_ID_EX_rd_out, u_IF_ID_rd, u_IF_ID_rs1, u_IF_ID_rs2,
       u_Mux_ControlSignals_exsignals_out;
  wire [6:0] u_IF_ID_func7;
  wire [31:0] RegFile_da, RegFile_db, u_EX_MEM_2_aluoutput_out, u_EX_MEM_2_datafrommem_out,
       u_EX_MEM_aluoutput_out, u_IF_ID_inst_out, u_IF_ID_pc_out, u_ImmGen_immediate, u_MemToReg_dataout,
       u_PCPlusFour_next_pc, u_PCPlusImm_next_pc, u_PCSrc_nextpc;

  PCSrc #(.applicationType("GHDL")) u_PCSrc (
    .PCplus4(u_PCPlusFour_next_pc), .ID_result(u_PCPlusImm_next_pc), .EX_result(VemDoEXStage), .S1(PCSrc1),
    .S2(PCSrc2), .NextPC(u_PCSrc_nextpc));
  PCPlusFour #(.applicationType("GHDL")) u_PCPlusFour (.PC(VaiVirarInstMem), .Next_PC(u_PCPlusFour_next_pc));
  Register #(.Bits(32)) PC (.D(u_PCSrc_nextpc), .C(Clock), .en(PCWrite), .Q(VaiVirarInstMem));
  IF_ID #(.applicationType("GHDL")) u_IF_ID (
    .PC_in(VaiVirarInstMem), .PC_out(u_IF_ID_pc_out), .inst_out(u_IF_ID_inst_out), .rd(u_IF_ID_rd),
    .rs1(u_IF_ID_rs1), .rs2(u_IF_ID_rs2), .func3(u_IF_ID_func3), .func7(u_IF_ID_func7));  // open: rst, clk, IF_ID_WRITE, IF_ID_flush, inst_in
  PCPlusImm #(.applicationType("GHDL")) u_PCPlusImm (
    .PC(u_IF_ID_pc_out), .IMM(u_ImmGen_immediate), .Next_PC(u_PCPlusImm_next_pc));
  RegisterFile #(.AddrBits(5), .Bits(32)) RegFile (
    .Din(u_MemToReg_dataout), .we(u_EX_MEM_2_regwrite), .Rw(u_EX_MEM_2_rd_out), .Ra(u_IF_ID_rs1),
    .Rb(u_IF_ID_rs2), .Da(RegFile_da), .Db(RegFile_db));  // open: C
  ImmGen #(.applicationType("GHDL")) u_ImmGen (.Instruction(u_IF_ID_inst_out), .Immediate(u_ImmGen_immediate));
  Mux_ControlSignals #(.applicationType("GHDL")) u_Mux_ControlSignals (
    .EXSignals_out(u_Mux_ControlSignals_exsignals_out), .MEMSignals_out(u_Mux_ControlSignals_memsignals_out),
    .WBSignals_out(u_Mux_ControlSignals_wbsignals_out));  // open: EXSignals_in, MEMSignals_in, WBSignals_in, stall
  CheckEqual #(.applicationType("GHDL")) u_CheckEqual (.Rs1(RegFile_da), .Rs2(RegFile_db), .IsEqual(BitIgualdade));
  ID_EX #(.applicationType("GHDL")) u_ID_EX (
    .EXSignals_in(u_Mux_ControlSignals_exsignals_out), .MEMSignals_in(u_Mux_ControlSignals_memsignals_out),
    .WBSignals_in(u_Mux_ControlSignals_wbsignals_out), .PC_in(u_IF_ID_pc_out), .rs1_data_in(RegFile_da),
    .rs2_data_in(RegFile_db), .rd_in(u_IF_ID_rd), .rs1_in(u_IF_ID_rs1), .rs2_in(u_IF_ID_rs2),
    .func3_in(u_IF_ID_func3), .func7_in(u_IF_ID_func7), .immediate_in(u_ImmGen_immediate),
    .rd_out(u_ID_EX_rd_out), .MEMSignals_out(u_ID_EX_memsignals_out), .WBSignals_out(u_ID_EX_wbsignals_out));  // open: rst, clk, rs1_data_out, rs2_data_out, PC_out, immediate_out, ALUSrcA, ALUSrcB, func3_out, func7_out, ALUOp, rs1_out, rs2_out
  Mux_4para1 #(.applicationType("GHDL")) u_Mux_4para1 ();  // open: D0, D1, D2, D3, SEL, Y
  ALUSrcA #(.applicationType("GHDL")) u_ALUSrcA ();  // open: Rs1, PC, SEL, A
  ALUSrcB #(.applicationType("GHDL")) u_ALUSrcB ();  // open: Rs2, imm, SEL, B
  EX_MEM #(.applicationType("GHDL")) u_EX_MEM (
    .rd_in(u_ID_EX_rd_out), .MEMSignals_in(u_ID_EX_memsignals_out), .WBSignals_in(u_ID_EX_wbsignals_out),
    .ALUoutput_out(u_EX_MEM_aluoutput_out), .rd_out(u_EX_MEM_rd_out), .WBSignals_out(u_EX_MEM_wbsignals_out));  // open: rst, clk, rs2_data_in, ALUoutput_in, rs2_data_out, MemRead, MemWrite
  EX_MEM #(.applicationType("GHDL")) u_EX_MEM_2 (
    .ALUoutput_in(u_EX_MEM_aluoutput_out), .rd_in(u_EX_MEM_rd_out), .WBSignals_in(u_EX_MEM_wbsignals_out),
    .rd_out(u_EX_MEM_2_rd_out), .DataFromMem_out(u_EX_MEM_2_datafrommem_out),
    .ALUoutput_out(u_EX_MEM_2_aluoutput_out), .MemToReg(u_EX_MEM_2_memtoreg), .RegWrite(u_EX_MEM_2_regwrite));  // open: rst, clk, DataFromMem_in
  MemToReg #(.applicationType("GHDL")) u_MemToReg (
    .MemOutput(u_EX_MEM_2_datafrommem_out), .ALUOutput(u_EX_MEM_2_aluoutput_out), .SEL(u_EX_MEM_2_memtoreg),
    .DataOut(u_MemToReg_dataout));
  // Pins of 1 and 32 bits meet at VaiVirarInstMem
  // Pins of 1 and 32 bits meet at VemDoEXStage
endmodule

/* Code of PCSrc:
library IEEE;
use IEEE.STD_LOGIC_1164.ALL;

entity PCSrc is
    Port (
        PCplus4 	: in  std_logic_vector(31 downto 0); -- Entrada de dados 0
        ID_result  	: in  std_logic_vector(31 downto 0); -- Entrada de dados 1
        EX_result	: in  std_logic_vector(31 downto 0); -- Entrada de dados 2
        S1 		: in  std_logic; -- Linha de seleção
        S2 		: in  std_logic; -- Linha de seleção
        NextPC 		: out std_logic_vector(31 downto 0)  -- Saída de dados
    );
end PCSrc;

architecture Behavorial of PCSrc is
signal SEL : std_logic_vector(1 downto 0);
begin
SEL <= S1&S2;
    process(PCplus4, ID_result, EX_result, S1, S2)
    begin
        case SEL is
            when "00"   => NextPC <= PCplus4;
            when "01"   => NextPC <= ID_result;
            when "10"   => NextPC <= EX_result;
            when others => NextPC <= (others => '0'); -- valores incorretos
        end case;
    end process;

end Behavorial;
*/

/* Code of PCPlusFour:
library IEEE;
use IEEE.STD_LOGIC_1164.ALL;
use IEEE.NUMERIC_STD.ALL;

entity PCPlusFour is
    Port (
        PC        : in  STD_LOGIC_VECTOR(31 downto 0);
        Next_PC   : out  STD_LOGIC_VECTOR(31 downto 0)
    );
end PCPlusFour;

architecture Behavioral of PCPlusFour is
begin
	Next_PC <= std_logic_vector(unsigned(PC) + 4);
end Behavioral;
*/

/* Code of IF_ID:
library IEEE;
use IEEE.STD_LOGIC_1164.ALL;

entity IF_ID is
    Port ( 
	rst     	: in  STD_LOGIC; 
        clk		: in  STD_LOGIC;

	IF_ID_WRITE	: in STD_LOGIC;
	IF_ID_flush	: in STD_LOGIC;
        PC_in		: in  STD_LOGIC_VECTOR(31 downto 0);
        inst_in		: in  STD_LOGIC_VECTOR(31 downto 0);

	PC_out		: out STD_LOGIC_VECTOR(31 downto 0);
	inst_out	: out STD_LOGIC_VECTOR(31 downto 0);
	rd		: out STD_LOGIC_VECTOR(4 downto 0);
        rs1		: out STD_LOGIC_VECTOR(4 downto 0);
        rs2		: out STD_LOGIC_VECTOR(4 downto 0);
	func3		: out STD_LOGIC_VECTOR(2 downto 0);
	func7		: out STD_LOGIC_VECTOR(6 downto 0)

    );
end IF_ID;

architecture Behavioral of IF_ID is

signal s_dado : STD_LOGIC_VECTOR(31 downto 0);

begin

process(clk,rst)
begin
	if rst = '1' then
		s_dado <= (others => '0');
        elsif rising_edge(clk) and IF_ID_WRITE='0' then
		if IF_ID_flush='1' then
			PC_out <= (others => '0');
			inst_out <= (others => '0');
		else
			PC_out <= PC_in;
            		inst_out <= inst_in;
		end if;
	end if;
end process;

rs1 <= inst_out(19 downto 15);
rs2 <= inst_out(24 downto 20);
rd <= inst_out(11 downto 7);
func3 <= inst_out(14 downto 12);
func7 <= inst_out(31 downto 25);

end Behavioral;
*/

/* Code of PCPlusImm:
library IEEE;
use IEEE.STD_LOGIC_1164.ALL;
use IEEE.NUMERIC_STD.ALL;

entity PCPlusImm is
    Port (
        PC        : in  STD_LOGIC_VECTOR(31 downto 0);
	IMM	  : in  STD_LOGIC_VECTOR(31 downto 0);
        Next_PC   : out  STD_LOGIC_VECTOR(31 downto 0)
    );
end PCPlusImm;

architecture Behavioral of PCPlusImm is
begin
	Next_PC <= std_logic_vector(unsigned(PC) + unsigned(IMM));
end Behavioral;
*/

/* Code of ImmGen:
library IEEE;
use IEEE.STD_LOGIC_1164.ALL;
use IEEE.NUMERIC_STD.ALL;

entity ImmGen is
    Port (
        Instruction	: in  STD_LOGIC_VECTOR(31 downto 0);
        Immediate   	: out  STD_LOGIC_VECTOR(31 downto 0)
    );
end ImmGen;

architecture Behavioral of ImmGen is

signal opcode : STD_LOGIC_VECTOR(6 downto 0);

begin

opcode <= Instruction(6 downto 0);

process(opcode)
begin
    case opcode is

        when "0110011" =>
		-- R type
		Immediate <= (others => '0');

        when "0010011" | "1100111" | "0000011" =>
		-- I type
		Immediate <= (others => Instruction (31));
		Immediate (11 downto 0) <= Instruction (31 downto 20);

        when "0010111" | "0110111" => 
            	-- U type
            	Immediate <= (others => '0');
		Immediate (31 downto 12) <= Instruction (31 downto 12);

        when "1100011" => 
            	-- SB type
		Immediate <= (others => Instruction (31));
		Immediate (0) <= '0';
		Immediate (11) <= Instruction (7);
		Immediate (4 downto 1) <= Instruction (11 downto 8);
		Immediate (10 downto 5) <= Instruction (30 downto 25);

        when "1101111" => 
            	-- UJ type
		Immediate <= (others => Instruction (31));
		Immediate (0) <= '0';
		Immediate (11) <= Instruction (20);
		Immediate (19 downto 12) <= Instruction (19 downto 12);
		Immediate (10 downto 1) <= Instruction (30 downto 21);
            	
        when "0100011" => 
           	 -- S type
            	Immediate <= (others => Instruction (31));
		Immediate (11 downto 5) <= Instruction (31 downto 25);
		Immediate (4 downto 0) <= Instruction (11 downto 7);

        when others =>
            	Immediate <= (others => '0');

    end case;
end process;

end Behavioral;
*/

/* Code of Mux_ControlSignals:
library IEEE;
use IEEE.STD_LOGIC_1164.ALL;

entity Mux_ControlSignals is
    Port (
        EXSignals_in	: in  STD_LOGIC_VECTOR(4 downto 0);
        MEMSignals_in	: in  STD_LOGIC_VECTOR(1 downto 0);
        WBSignals_in	: in  STD_LOGIC_VECTOR(1 downto 0);
        stall		: in  std_logic;
        EXSignals_out	: out STD_LOGIC_VECTOR(4 downto 0);
        MEMSignals_out	: out STD_LOGIC_VECTOR(1 downto 0);
        WBSignals_out	: out STD_LOGIC_VECTOR(1 downto 0)
    );
end Mux_ControlSignals;

architecture Behavorial of Mux_ControlSignals is
begin
    process(EXSignals_in, MEMSignals_in, WBSignals_in, stall)
    begin
        case stall is
            when '0' => 
		EXSignals_out <= EXSignals_in;
		MEMSignals_out <= MEMSignals_in;
		WBSignals_out <= WBSignals_in;
            when others =>
		EXSignals_out <= (others => '0');
		MEMSignals_out <= (others => '0');
		WBSignals_out <= (others => '0');
        end case;
    end process;

end Behavorial;
*/

/* Code of CheckEqual:
library IEEE;
use IEEE.STD_LOGIC_1164.ALL;
use IEEE.NUMERIC_STD.ALL;

entity CheckEqual is
    Port (
        Rs1        : in  STD_LOGIC_VECTOR(31 downto 0);
	Rs2	  : in  STD_LOGIC_VECTOR(31 downto 0);
        IsEqual   : out  STD_LOGIC
    );
end CheckEqual;

architecture Behavioral of CheckEqual is
begin
	IsEqual <= '1' when Rs1 = Rs2 else '0';
end Behavioral;
*/

/* Code of ID_EX:
library IEEE;
use IEEE.STD_LOGIC_1164.ALL;

entity ID_EX is
    Port ( 
	rst     	: in  STD_LOGIC; 
        clk		: in  STD_LOGIC;

        EXSignals_in	: in  STD_LOGIC_VECTOR(4 downto 0);
        MEMSignals_in	: in  STD_LOGIC_VECTOR(1 downto 0);
        WBSignals_in	: in  STD_LOGIC_VECTOR(1 downto 0);

	PC_in		: in STD_LOGIC_VECTOR(31 downto 0);
        rs1_data_in	: in  STD_LOGIC_VECTOR(31 downto 0);
        rs2_data_in	: in  STD_LOGIC_VECTOR(31 downto 0);
        rd_in		: in  STD_LOGIC_VECTOR(4 downto 0);
        rs1_in		: in  STD_LOGIC_VECTOR(4 downto 0);
        rs2_in		: in  STD_LOGIC_VECTOR(4 downto 0);
	func3_in	: in STD_LOGIC_VECTOR(2 downto 0);
	func7_in	: in STD_LOGIC_VECTOR(6 downto 0);
        immediate_in	: in  STD_LOGIC_VECTOR(31 downto 0);

        rs1_data_out	: out STD_LOGIC_VECTOR(31 downto 0);
        rs2_data_out	: out STD_LOGIC_VECTOR(31 downto 0);
	PC_out		: out STD_LOGIC_VECTOR(31 downto 0);
	immediate_out	: out STD_LOGIC_VECTOR(31 downto 0);
	ALUSrcA		: out STD_LOGIC_VECTOR(1 downto 0);
	ALUSrcB		: out STD_LOGIC;
	func3_out	: out STD_LOGIC_VECTOR(2 downto 0);
	func7_out	: out STD_LOGIC_VECTOR(6 downto 0);
	ALUOp		: out STD_LOGIC_VECTOR(1 downto 0);
	rs1_out		: out STD_LOGIC_VECTOR(4 downto 0);
	rs2_out		: out STD_LOGIC_VECTOR(4 downto 0);
	rd_out		: out STD_LOGIC_VECTOR(4 downto 0);
	MEMSignals_out	: out STD_LOGIC_VECTOR(1 downto 0);
	WBSignals_out	: out STD_LOGIC_VECTOR(1 downto 0)
    );
end ID_EX;

architecture Behavioral of ID_EX is

signal s_dado : STD_LOGIC_VECTOR(31 downto 0);

begin

process(clk,rst)
begin
	if rst = '1' then
		rs1_out <= (others => '0');
		rs2_out <= (others => '0');
		rd_out <= (others => '0');
		rs1_data_out <= (others => '0');
		rs2_data_out <= (others => '0');
		func3_out <= (others => '0');
		func7_out <= (others => '0');
		immediate_out <= (others => '0');
		ALUSrcA <= (others => '0');
		ALUSrcB <= '0';
		ALUOp <= (others => '0');
		MEMSignals_out <= (others => '0');
		WBSignals_out <= (others => '0');
        elsif rising_edge(clk) then
		rs1_out <= rs1_in;
		rs2_out <= rs2_in;
		rd_out <= rd_in;
		rs1_data_out <= rs1_data_in;
		rs2_data_out <= rs2_data_in;
		func3_out <= func3_in;
		func7_out <= func7_in;
		immediate_out <= immediate_in;
		ALUSrcA <= EXSignals_in(1 downto 0);
		ALUSrcB <= EXSignals_in(2);
		ALUOp <= EXSignals_in(4 downto 3);
		MEMSignals_out <= MEMSignals_in;
		WBSignals_out <= WBSignals_in;
	end if;
end process;

end Behavioral;
*/

/* Code of Mux_4para1:
library IEEE;
use IEEE.STD_LOGIC_1164.ALL;

entity Mux_4para1 is
    Port (
        D0  : in  std_logic_vector(1 downto 0); -- Entrada de dados 0
        D1  : in  std_logic_vector(1 downto 0); -- Entrada de dados 1
        D2  : in  std_logic_vector(1 downto 0); -- Entrada de dados 2
        D3  : in  std_logic_vector(1 downto 0); -- Entrada de dados 3
        SEL : in  std_logic_vector(1 downto 0); -- Linha de seleção de 2 bits
        Y   : out std_logic_vector(1 downto 0)  -- Saída de dados
    );
end Mux_4para1;

architecture Behavorial of Mux_4para1 is
begin
    process(D0, D1, D2, D3, SEL)
    begin
        case SEL is
            when "00"   => Y <= D0;
            when "01"   => Y <= D1;
            when "10"   => Y <= D2;
            when others => Y <= D3; -- Cobre o caso "11" e outros possíveis (U, X, etc.)
        end case;
    end process;

end Behavorial;
*/

/* Code of ALUSrcA:
library IEEE;
use IEEE.STD_LOGIC_1164.ALL;

entity ALUSrcA is
    Port (
        Rs1  	: in  std_logic_vector(31 downto 0); -- Entrada de dados 0
        PC  	: in  std_logic_vector(31 downto 0); -- Entrada de dados 1
        SEL 	: in  std_logic_vector(1 downto 0); -- Linha de seleção de 2 bits
        A   	: out std_logic_vector(31 downto 0)  -- Saída de dados
    );
end ALUSrcA;

architecture Behavorial of ALUSrcA is
begin
    process(Rs1, PC, SEL)
    begin
        case SEL is
            when "00"   => A <= Rs1;
            when "01"   => A <= PC;
            when others => A <= (others => '0'); -- "10" e sinais incorretos
        end case;
    end process;

end Behavorial;
*/

/* Code of ALUSrcB:
library IEEE;
use IEEE.STD_LOGIC_1164.ALL;

entity ALUSrcB is
    Port (
        Rs2  	: in  std_logic_vector(31 downto 0); -- Entrada de dados 0
        imm  	: in  std_logic_vector(31 downto 0); -- Entrada de dados 1
        SEL 	: in  std_logic; -- Linha de seleção
        B   	: out std_logic_vector(31 downto 0)  -- Saída de dados
    );
end ALUSrcB;

architecture Behavorial of ALUSrcB is
begin
    process(Rs2, imm, SEL)
    begin
        case SEL is
            when '0'   => B <= Rs2;
            when others => B <= imm; -- '1'
        end case;
    end process;

end Behavorial;
*/

/* Code of EX_MEM:
library IEEE;
use IEEE.STD_LOGIC_1164.ALL;

entity EX_MEM is
    Port ( 
	rst     	: in  STD_LOGIC; 
        clk		: in  STD_LOGIC;

        rs2_data_in	: in  STD_LOGIC_VECTOR(31 downto 0); --for store instruction
	ALUoutput_in	: in  STD_LOGIC_VECTOR(31 downto 0);
        rd_in		: in  STD_LOGIC_VECTOR(4 downto 0);

	MEMSignals_in	: in STD_LOGIC_VECTOR(1 downto 0);
	WBSignals_in	: in STD_LOGIC_VECTOR(1 downto 0);

        rs2_data_out	: out STD_LOGIC_VECTOR(31 downto 0);
	MemRead		: out STD_LOGIC;
	MemWrite	: out STD_LOGIC;
	ALUoutput_out	: out  STD_LOGIC_VECTOR(31 downto 0);
	rd_out		: out STD_LOGIC_VECTOR(4 downto 0);
	WBSignals_out	: out STD_LOGIC_VECTOR(1 downto 0)
    );
end EX_MEM;

architecture Behavioral of EX_MEM is

signal s_dado : STD_LOGIC_VECTOR(31 downto 0);

begin

process(clk,rst)
begin
	if rst = '1' then
		rd_out <= (others => '0');
		rs2_data_out <= (others => '0');
		ALUoutput_out <= (others => '0');
		MemRead <= '0';
		MemWrite <= '0';
		WBSignals_out <= (others => '0');
        elsif rising_edge(clk) then
		rd_out <= rd_in;
		rs2_data_out <= rs2_data_in;
		ALUoutput_out <= ALUoutput_in;
		MemRead <= MEMSignals_in(0);
		MemWrite <= MEMSignals_in(1);
		WBSignals_out <= WBSignals_in;
	end if;
end process;

end Behavioral;
*/

/* Code of EX_MEM:
library IEEE;
use IEEE.STD_LOGIC_1164.ALL;

entity EX_MEM is
    Port ( 
	rst     	: in  STD_LOGIC; 
        clk		: in  STD_LOGIC;

        DataFromMem_in	: in  STD_LOGIC_VECTOR(31 downto 0);
	ALUoutput_in	: in  STD_LOGIC_VECTOR(31 downto 0);
        rd_in		: in  STD_LOGIC_VECTOR(4 downto 0);

	WBSignals_in	: in STD_LOGIC_VECTOR(1 downto 0);

	rd_out		: out STD_LOGIC_VECTOR(4 downto 0);
        DataFromMem_out	: out STD_LOGIC_VECTOR(31 downto 0);
	ALUoutput_out	: out  STD_LOGIC_VECTOR(31 downto 0);

	MemToReg 	: out STD_LOGIC;
	RegWrite 	: out STD_LOGIC
    );
end EX_MEM;

architecture Behavioral of EX_MEM is

signal s_dado : STD_LOGIC_VECTOR(31 downto 0);

begin

process(clk,rst)
begin
	if rst = '1' then
		rd_out <= (others => '0');
		DataFromMem_out <= (others => '0');
		ALUoutput_out <= (others => '0');
		MemToReg <= '0';
		RegWrite <= '0';
        elsif rising_edge(clk) then
		rd_out <= rd_in;
		DataFromMem_out <= DataFromMem_in;
		ALUoutput_out <= ALUoutput_in;
		MemToReg <= WBSignals_in(0);
		RegWrite <= WBSignals_in(1);
	end if;
end process;

end Behavioral;
*/

/* Code of MemToReg:
library IEEE;
use IEEE.STD_LOGIC_1164.ALL;

entity MemToReg is
    Port (
        MemOutput	: in  std_logic_vector(31 downto 0); -- Entrada de dados 0
        ALUOutput	: in  std_logic_vector(31 downto 0); -- Entrada de dados 1
        SEL		: in  std_logic; -- Linha de seleção
        DataOut		: out std_logic_vector(31 downto 0)  -- Saída de dados
    );
end MemToReg;

architecture Behavorial of MemToReg is
begin
    process(MemOutput, ALUOutput, SEL)
    begin
        case SEL is
            when '0'   => DataOut <= MemOutput;
            when '1'   => DataOut <= ALUOutput;
            when others => DataOut <= (others => '0'); -- Cobre o caso "11" e outros possíveis (U, X, etc.)
        end case;
    end process;

end Behavorial;
*/
